// Logisim project plasek0.circ as structural Verilog: 1 circuit, main circuit main
module main (
  input  x0,
  input  x1,
  input  s,
  output y
);

  wire not_1_out;

  assign y = not_1_out ? x0 : 1'bz;  // Controlled_Buffer controlled_buffer_1
  not not_1 (not_1_out, s);
  assign y = s ? x1 : 1'bz;  // Controlled_Buffer controlled_buffer_2
endmodule
