// Logisim project plasek1.circ as structural Verilog: 1 circuit, main circuit main
module main (
  input  x0,
  input  x1,
  output c,
  output s
);

  and and_1 (c, x0, x1);
  xor xor_1 (s, x0, x1);
endmodule
