// Logisim project plasek2.circ as structural Verilog: 1 circuit, main circuit main
module main (
  input  cin,
  input  x0,
  input  x1,
  output s,
  output C
);

  wire and_1_out, and_2_out, not_1_out, or_1_out, xor_1_out;

  xor xor_1 (xor_1_out, cin, x0);
  xor xor_2 (s, xor_1_out, x1);
  not not_1 (not_1_out, s);
  or or_1 (or_1_out, cin, x0, x1);
  and and_1 (and_1_out, or_1_out, not_1_out);
  and and_2 (and_2_out, cin, x0, x1);
  or or_2 (C, and_1_out, and_2_out);
endmodule
