// Logisim project plasek3.circ as structural Verilog: 1 circuit, main circuit main
module main (
  output Q,
  output Qp
);

  wire R_out, S_out;

  Button R (.out(R_out));
  Button S (.out(S_out));
  Pull_Resistor pull_resistor_1 (.node(Q));
  nor nor_1 (Q, R_out, Qp);
  nor nor_2 (Qp, Q, S_out);
endmodule
