// Logisim project plasek4.circ as structural Verilog: 1 circuit, main circuit main
module main (
  input  x0,
  input  x1,
  input  x2,
  input  x3,
  input  s0,
  input  s1,
  output y
);

  wire controlled_buffer_1_out, controlled_buffer_2_out, not_1_out, not_2_out;

  assign controlled_buffer_1_out = s0 ? x1 : 1'bz;  // Controlled_Buffer controlled_buffer_1
  assign controlled_buffer_2_out = s0 ? x3 : 1'bz;  // Controlled_Buffer controlled_buffer_2
  assign controlled_buffer_1_out = not_1_out ? x0 : 1'bz;  // Controlled_Buffer controlled_buffer_3
  assign controlled_buffer_2_out = not_1_out ? x2 : 1'bz;  // Controlled_Buffer controlled_buffer_4
  not not_1 (not_1_out, s0);
  assign y = not_2_out ? controlled_buffer_1_out : 1'bz;  // Controlled_Buffer controlled_buffer_5
  assign y = s1 ? controlled_buffer_2_out : 1'bz;  // Controlled_Buffer controlled_buffer_6
  not not_2 (not_2_out, s1);
endmodule
